// Logisim project RAMBinaryCell.circ as structural Verilog: 2 circuits, main circuit main
// Read/Write'
module main (
  input  in_1,
  input  in_2,
  input  in_3,
  input  in_4,
  input  [2:0] in_5,
  input  [1:0] in_6,
  input  [1:0] in_7,
  input  in_8,
  input  in_9,
  input  in_10,
  input  in_11,
  output out_12,
  output out_13,
  output out_14
);

  wire binarycell_1_output, binarycell_2_output, binarycell_3_output, binarycell_4_output,
       binarycell_5_output, binarycell_6_output, binarycell_7_output, binarycell_8_output,
       binarycell_9_output, binarycell_10_output, binarycell_11_output, binarycell_12_output, clock_1_out,
       decoder_1_out0, decoder_1_out1, decoder_1_out2, decoder_1_out3;

  Decoder #(.select(2)) decoder_1 (
    .out0(decoder_1_out0), .out1(decoder_1_out1), .out2(decoder_1_out2), .out3(decoder_1_out3), .sel(in_7),
    .en(in_4));
  binaryCell binarycell_1 (.Input(in_1), .Output(binarycell_1_output), .R_W_prime(in_11), .Select(decoder_1_out0));
  binaryCell binarycell_2 (.Input(in_1), .Output(binarycell_2_output), .R_W_prime(in_11), .Select(decoder_1_out1));
  binaryCell binarycell_3 (.Input(in_1), .Output(binarycell_3_output), .R_W_prime(in_11), .Select(decoder_1_out2));
  binaryCell binarycell_4 (.Input(in_1), .Output(binarycell_4_output), .R_W_prime(in_11), .Select(decoder_1_out3));
  or or_1 (out_12, binarycell_4_output, binarycell_3_output, binarycell_2_output, binarycell_1_output);
  binaryCell binarycell_5 (.Input(in_2), .Output(binarycell_5_output), .R_W_prime(in_11), .Select(decoder_1_out0));
  binaryCell binarycell_6 (.Input(in_2), .Output(binarycell_6_output), .R_W_prime(in_11), .Select(decoder_1_out1));
  binaryCell binarycell_7 (.Input(in_2), .Output(binarycell_7_output), .R_W_prime(in_11), .Select(decoder_1_out2));
  binaryCell binarycell_8 (.Input(in_2), .Output(binarycell_8_output), .R_W_prime(in_11), .Select(decoder_1_out3));
  or or_2 (out_13, binarycell_8_output, binarycell_7_output, binarycell_6_output, binarycell_5_output);
  binaryCell binarycell_9 (.Input(in_3), .Output(binarycell_9_output), .R_W_prime(in_11), .Select(decoder_1_out0));
  binaryCell binarycell_10 (.Input(in_3), .Output(binarycell_10_output), .R_W_prime(in_11), .Select(decoder_1_out1));
  binaryCell binarycell_11 (.Input(in_3), .Output(binarycell_11_output), .R_W_prime(in_11), .Select(decoder_1_out2));
  binaryCell binarycell_12 (.Input(in_3), .Output(binarycell_12_output), .R_W_prime(in_11), .Select(decoder_1_out3));
  or or_3 (out_14, binarycell_12_output, binarycell_11_output, binarycell_10_output, binarycell_9_output);
  Clock clock_1 (.out(clock_1_out));
  RAM #(.addrWidth(2), .dataWidth(3)) ram_1 (
    .addr(in_6), .data(in_5), .sel(in_9), .clk(clock_1_out), .ld(in_10));  // open: clr

  // Notes on the sheet:
  //   R/W'
endmodule

module binaryCell (
  input  R_W_prime,
  input  Input,
  input  Select,
  output Output
);

  wire and_1_out, and_2_out, nor_1_out, nor_2_out, not_1_out, not_2_out;

  not not_1 (not_1_out, Input);
  not not_2 (not_2_out, R_W_prime);
  and and_1 (and_1_out, not_2_out, Input, Select);
  and and_2 (and_2_out, not_2_out, not_1_out, Select);
  nor nor_1 (nor_1_out, and_1_out, nor_2_out);
  nor nor_2 (nor_2_out, nor_1_out, and_2_out);
  and and_3 (Output, R_W_prime, nor_2_out, Select);

  // Notes on the sheet:
  //   S
  //   R
  //   Q
endmodule
